// Logisim project Automat_PSN.circ as structural Verilog: 3 circuits, main circuit Automat
module Automat (
  input  min
);

  wire and_1_out, and_2_out, clock_1_out, clock_2_out, comparator_1_eq, comparator_2_eq, comparator_3_eq,
       comparator_4_eq, comparator_5_eq, comparator_6_eq, comparator_7_eq, comparator_8_eq, grade_out,
       luna_out, or_1_out, or_2_out, or_3_out, ora_out, zi_out;
  wire [6:0] bcd7segm_1_out_2, bcd7segm_2_out_2, bcd7segm_3_out_2, bcd7segm_4_out_2, bcd7segm_5_out_2;
  wire [7:0] adder_1_out, counter_1_q, counter_2_q, counter_3_q, counter_4_q, counter_5_q;

  Button zi (.out(zi_out));
  Button grade (.out(grade_out));
  Button luna (.out(luna_out));
  Clock clock_1 (.out(clock_1_out));
  or or_1 (or_1_out, comparator_1_eq, zi_out, comparator_7_eq);
  Button ora (.out(ora_out));
  Clock clock_2 (.out(clock_2_out));
  or or_2 (or_2_out, comparator_2_eq, luna_out, comparator_6_eq);
  Counter #(.max('h1e)) counter_1 (.count(or_1_out), .Q(counter_1_q), .clk(clock_1_out));  // open: load, D, carry, clr
  or or_3 (or_3_out, ora_out, comparator_4_eq);
  Counter #(.max('h3b)) counter_2 (.count(min), .Q(counter_2_q), .clk(clock_2_out));  // open: load, D, carry, clr
  Counter #(.max('h3b)) counter_3 (.count(grade_out), .Q(counter_3_q), .clk(clock_2_out));  // open: load, D, carry, clr
  Counter #(.max('hc)) counter_4 (.count(or_2_out), .Q(counter_4_q), .clk(clock_1_out));  // open: load, D, carry, clr
  Comparator comparator_1 (.a({8{1'b0}}), .b(counter_1_q), .eq(comparator_1_eq));  // open: gt, lt
  // Probe on counter_5_q
  Counter #(.max('h17)) counter_5 (.count(or_3_out), .Q(counter_5_q), .clk(clock_2_out));  // open: load, D, carry, clr
  // Probe on counter_2_q
  // Probe on counter_3_q
  Comparator comparator_2 (.a({8{1'b0}}), .b(counter_4_q), .eq(comparator_2_eq));  // open: gt, lt
  // Probe on counter_1_q
  // Probe on counter_4_q
  Comparator comparator_3 (.a(counter_5_q), .b(8'h17), .eq(comparator_3_eq));  // open: gt, lt
  Comparator comparator_4 (.a(counter_2_q), .b(8'h3b), .eq(comparator_4_eq));  // open: gt, lt
  BCD7segm bcd7segm_1 (.in_1(counter_3_q), .out_2(bcd7segm_1_out_2));
  Comparator comparator_5 (.a(8'h1e), .b(counter_1_q), .eq(comparator_5_eq));  // open: gt, lt
  BCD7segm bcd7segm_2 (.in_1(counter_4_q), .out_2(bcd7segm_2_out_2));
  and and_1 (and_1_out, comparator_5_eq, comparator_8_eq);
  and and_2 (and_2_out, comparator_3_eq, comparator_4_eq);
  // Probe on adder_1_out
  Adder adder_1 (.a(counter_5_q), .b(counter_2_q), .out(adder_1_out));  // open: cin, cout
  Comparator #(.width(1)) comparator_6 (.a(1'b1), .b(and_1_out), .eq(comparator_6_eq));  // open: gt, lt
  Comparator #(.width(1)) comparator_7 (.a(1'b1), .b(and_2_out), .eq(comparator_7_eq));  // open: gt, lt
  Comparator comparator_8 (.a(adder_1_out), .b(8'h52), .eq(comparator_8_eq));  // open: gt, lt
  _7_Segment_Display u_7_segment_display_1 (
    .g(bcd7segm_2_out_2[6]), .f(bcd7segm_2_out_2[5]), .a(bcd7segm_2_out_2[0]), .b(bcd7segm_2_out_2[1]),
    .e(bcd7segm_2_out_2[4]), .d(bcd7segm_2_out_2[3]), .c(bcd7segm_2_out_2[2]));  // open: dp
  BCD7segm bcd7segm_3 (.in_1(counter_1_q), .out_2(bcd7segm_3_out_2));
  BCD7segm bcd7segm_4 (.in_1(counter_5_q), .out_2(bcd7segm_4_out_2));
  BCD7segm bcd7segm_5 (.in_1(counter_2_q), .out_2(bcd7segm_5_out_2));
  _7_Segment_Display u_7_segment_display_2 (
    .g(bcd7segm_1_out_2[6]), .f(bcd7segm_1_out_2[5]), .a(bcd7segm_1_out_2[0]), .b(bcd7segm_1_out_2[1]),
    .e(bcd7segm_1_out_2[4]), .d(bcd7segm_1_out_2[3]), .c(bcd7segm_1_out_2[2]));  // open: dp
  _7_Segment_Display u_7_segment_display_3 (
    .g(bcd7segm_2_out_2[6]), .f(bcd7segm_2_out_2[5]), .a(bcd7segm_2_out_2[0]), .b(bcd7segm_2_out_2[1]),
    .e(bcd7segm_2_out_2[4]), .d(bcd7segm_2_out_2[3]), .c(bcd7segm_2_out_2[2]));  // open: dp
  _7_Segment_Display u_7_segment_display_4 (
    .g(bcd7segm_4_out_2[6]), .f(bcd7segm_4_out_2[5]), .a(bcd7segm_4_out_2[0]), .b(bcd7segm_4_out_2[1]),
    .e(bcd7segm_4_out_2[4]), .d(bcd7segm_4_out_2[3]), .c(bcd7segm_4_out_2[2]));  // open: dp
  _7_Segment_Display u_7_segment_display_5 (
    .g(bcd7segm_1_out_2[6]), .f(bcd7segm_1_out_2[5]), .a(bcd7segm_1_out_2[0]), .b(bcd7segm_1_out_2[1]),
    .e(bcd7segm_1_out_2[4]), .d(bcd7segm_1_out_2[3]), .c(bcd7segm_1_out_2[2]));  // open: dp
  _7_Segment_Display u_7_segment_display_6 (
    .g(bcd7segm_3_out_2[6]), .f(bcd7segm_3_out_2[5]), .a(bcd7segm_3_out_2[0]), .b(bcd7segm_3_out_2[1]),
    .e(bcd7segm_3_out_2[4]), .d(bcd7segm_3_out_2[3]), .c(bcd7segm_3_out_2[2]));  // open: dp
  _7_Segment_Display u_7_segment_display_7 (
    .g(bcd7segm_4_out_2[6]), .f(bcd7segm_4_out_2[5]), .a(bcd7segm_4_out_2[0]), .b(bcd7segm_4_out_2[1]),
    .e(bcd7segm_4_out_2[4]), .d(bcd7segm_4_out_2[3]), .c(bcd7segm_4_out_2[2]));  // open: dp
  _7_Segment_Display u_7_segment_display_8 (
    .g(bcd7segm_3_out_2[6]), .f(bcd7segm_3_out_2[5]), .a(bcd7segm_3_out_2[0]), .b(bcd7segm_3_out_2[1]),
    .e(bcd7segm_3_out_2[4]), .d(bcd7segm_3_out_2[3]), .c(bcd7segm_3_out_2[2]));  // open: dp
  _7_Segment_Display u_7_segment_display_9 (
    .g(bcd7segm_5_out_2[6]), .f(bcd7segm_5_out_2[5]), .a(bcd7segm_5_out_2[0]), .b(bcd7segm_5_out_2[1]),
    .e(bcd7segm_5_out_2[4]), .d(bcd7segm_5_out_2[3]), .c(bcd7segm_5_out_2[2]));  // open: dp
  _7_Segment_Display u_7_segment_display_10 (
    .g(bcd7segm_5_out_2[6]), .f(bcd7segm_5_out_2[5]), .a(bcd7segm_5_out_2[0]), .b(bcd7segm_5_out_2[1]),
    .e(bcd7segm_5_out_2[4]), .d(bcd7segm_5_out_2[3]), .c(bcd7segm_5_out_2[2]));  // open: dp

  // Notes on the sheet:
  //   exc7
  //   exc4
  //   clk
  //   exc2
  //   in_zi
  //   OR3_2
  //   exc6
  //   OR2
  //   clk
  //   in_minut
  //   clk
  //   clk
  //   in_grade
  //   exc1
  //   OR3_1
  //   in_luna
  //   clk
  //   ex_zi
  //   counter2
  //   in_ora
  //   clk
  //   counter4
  //   ex_minut.
  //   counter5
  //   comparator1
  //   ex_luna
  //   ex_luna
  //   counter1
  //   exc2
  //   comparator2
  //   counter3
  //   ex_ora
  //   ex_grade
  //   ex_grade
  //   comparator3
  //   comparator5
  //   comparator6
  //   exc6
  //   ex_minut
  //   BCD7seg_5
  //   ex_luna
  //   exc3
  //   exc8
  //   exc5
  //   exc6
  //   ex_ora
  //   ex_bcd5
  //   BCD7seg_1
  //   exA2_1
  //   AND2_1
  //   exc5
  //   exA2_2
  //   AND2_2
  //   ex_sum
  //   sumator
  //   ex_bcd1
  //   comparator4
  //   exc4
  //   exc7
  //   comparator7
  //   comparator8
  //   exc8
  //   BCD7seg_2
  //   ex_zi
  //   ex_ora
  //   ex_minut.
  //   ex_bcd2
  //   BCD7seg_3
  //   BCD7seg_4
  //   ex_bcd3
  //   ex_bcd4
endmodule

module BCD7segm (
  input  [7:0] in_1,
  output [6:0] out_2
);

  wire and_1_out, and_2_out, and_3_out, and_4_out, and_5_out, and_6_out, and_7_out, and_8_out, and_9_out,
       and_10_out, and_11_out, and_12_out, and_13_out, and_14_out, and_15_out, and_16_out, not_1_out,
       not_2_out, not_3_out, not_4_out, not_5_out, not_6_out, not_7_out, not_8_out, not_9_out, not_10_out,
       not_11_out, not_12_out, not_13_out, not_14_out, not_15_out, not_16_out, not_17_out, not_18_out,
       not_19_out, not_20_out, not_21_out;

  not not_1 (not_1_out, in_1[2]);
  not not_2 (not_2_out, in_1[0]);
  not not_3 (not_3_out, in_1[1]);
  not not_4 (not_4_out, in_1[0]);
  not not_5 (not_5_out, in_1[1]);
  not not_6 (not_6_out, in_1[2]);
  not not_7 (not_7_out, in_1[0]);
  not not_8 (not_8_out, in_1[2]);
  not not_9 (not_9_out, in_1[0]);
  not not_10 (not_10_out, in_1[1]);
  not not_11 (not_11_out, in_1[2]);
  not not_12 (not_12_out, in_1[0]);
  not not_13 (not_13_out, in_1[0]);
  not not_14 (not_14_out, in_1[1]);
  not not_15 (not_15_out, in_1[0]);
  not not_16 (not_16_out, in_1[1]);
  not not_17 (not_17_out, in_1[0]);
  not not_18 (not_18_out, in_1[2]);
  not not_19 (not_19_out, in_1[1]);
  not not_20 (not_20_out, in_1[0]);
  and and_1 (and_1_out, not_1_out, not_2_out);
  and and_2 (and_2_out, in_1[2], in_1[0]);
  not not_21 (not_21_out, in_1[2]);
  and and_3 (and_3_out, not_3_out, not_4_out);
  and and_4 (and_4_out, in_1[1], in_1[0]);
  or or_1 (out_2[2], not_5_out, in_1[0], in_1[2]);
  and and_5 (and_5_out, not_6_out, not_7_out);
  and and_6 (and_6_out, not_8_out, in_1[1]);
  and and_7 (and_7_out, in_1[1], not_9_out);
  and and_8 (and_8_out, in_1[2], not_10_out, in_1[0]);
  and and_9 (and_9_out, not_11_out, not_12_out);
  and and_10 (and_10_out, in_1[1], not_13_out);
  and and_11 (and_11_out, not_14_out, not_15_out);
  and and_12 (and_12_out, in_1[2], not_16_out);
  and and_13 (and_13_out, in_1[2], not_17_out);
  and and_14 (and_14_out, not_18_out, in_1[1]);
  and and_15 (and_15_out, in_1[2], not_19_out);
  and and_16 (and_16_out, in_1[2], not_20_out);
  or or_2 (out_2[0], and_1_out, in_1[1], and_2_out, in_1[3]);
  or or_3 (out_2[1], not_21_out, and_3_out, and_4_out);
  or or_4 (out_2[3], and_5_out, and_6_out, and_7_out, and_8_out, in_1[3]);
  or or_5 (out_2[4], and_9_out, and_10_out);
  or or_6 (out_2[5], and_11_out, and_12_out, and_13_out, in_1[3]);
  or or_7 (out_2[6], and_14_out, and_15_out, and_16_out, in_1[3]);
endmodule

module Final (
  input  in_1,
  input  min,
  input  in_3
);

  wire and_1_out, and_2_out, clock_1_out, clock_2_out, clock_3_out, comparator_1_eq, comparator_2_eq,
       comparator_3_eq, comparator_4_eq, comparator_5_eq, comparator_6_eq, comparator_7_eq, comparator_8_eq,
       luna_out, or_1_out, or_2_out, or_3_out, ora_out, zi_out;
  wire [2:0] counter_6_q;
  wire [6:0] AND2_3_out, AND2_4_out, AND2_5_out, AND2_6_out, AND2_7_out, AND2_8_out, AND2_9_out, AND2_10_out,
       bcd7segm_1_out_2, demultiplexer_1_out0, demultiplexer_1_out1, demultiplexer_1_out2,
       demultiplexer_1_out3, demultiplexer_1_out4, demultiplexer_1_out5, demultiplexer_1_out6,
       demultiplexer_1_out7;
  wire [7:0] adder_1_out, counter_1_q, counter_2_q, counter_3_q, counter_4_q, counter_5_q, multiplexer_1_out;

  Button zi (.out(zi_out));
  Button grade (.out(in_3));
  Button luna (.out(luna_out));
  Clock clock_1 (.out(clock_1_out));
  or or_1 (or_1_out, comparator_1_eq, zi_out, comparator_7_eq);
  Button ora (.out(ora_out));
  Clock clock_2 (.out(clock_2_out));
  or or_2 (or_2_out, comparator_2_eq, luna_out, comparator_6_eq);
  Counter #(.max('h1e)) counter_1 (.count(or_1_out), .Q(counter_1_q), .clk(clock_1_out));  // open: load, D, carry, clr
  or or_3 (or_3_out, ora_out, comparator_4_eq);
  Counter #(.max('h3b)) counter_2 (.count(min), .Q(counter_2_q), .clk(clock_2_out));  // open: load, D, carry, clr
  Counter #(.max('h3b)) counter_3 (.count(in_3), .Q(counter_3_q), .clk(clock_2_out));  // open: load, D, carry, clr
  Counter #(.max('hc)) counter_4 (.count(or_2_out), .Q(counter_4_q), .clk(clock_1_out));  // open: load, D, carry, clr
  Comparator comparator_1 (.a({8{1'b0}}), .b(counter_1_q), .eq(comparator_1_eq));  // open: gt, lt
  // Probe on counter_5_q
  Counter #(.max('h17)) counter_5 (.count(or_3_out), .Q(counter_5_q), .clk(clock_2_out));  // open: load, D, carry, clr
  // Probe on counter_2_q
  // Probe on counter_3_q
  Comparator comparator_2 (.a({8{1'b0}}), .b(counter_4_q), .eq(comparator_2_eq));  // open: gt, lt
  // Probe on counter_1_q
  // Probe on counter_4_q
  Comparator comparator_3 (.a(counter_5_q), .b(8'h17), .eq(comparator_3_eq));  // open: gt, lt
  Comparator comparator_4 (.a(counter_2_q), .b(8'h3b), .eq(comparator_4_eq));  // open: gt, lt
  Comparator comparator_5 (.a(8'h1e), .b(counter_1_q), .eq(comparator_5_eq));  // open: gt, lt
  and and_1 (and_1_out, comparator_5_eq, comparator_8_eq);
  and and_2 (and_2_out, comparator_3_eq, comparator_4_eq);
  // Probe on adder_1_out
  Adder adder_1 (.a(counter_5_q), .b(counter_2_q), .out(adder_1_out));  // open: cin, cout
  Comparator #(.width(1)) comparator_6 (.a(1'b1), .b(and_1_out), .eq(comparator_6_eq));  // open: gt, lt
  Comparator #(.width(1)) comparator_7 (.a(1'b1), .b(and_2_out), .eq(comparator_7_eq));  // open: gt, lt
  Comparator comparator_8 (.a(adder_1_out), .b(8'h52), .eq(comparator_8_eq));  // open: gt, lt
  Counter #(.width(3), .max('h7)) counter_6 (.Q(counter_6_q), .clk(clock_3_out));  // open: load, D, count, carry, clr
  Clock clock_3 (.out(clock_3_out));
  Demultiplexer #(.select(3), .width(7)) demultiplexer_1 (
    .out0(demultiplexer_1_out0), .out1(demultiplexer_1_out1), .out2(demultiplexer_1_out2),
    .out3(demultiplexer_1_out3), .out4(demultiplexer_1_out4), .out5(demultiplexer_1_out5),
    .out6(demultiplexer_1_out6), .out7(demultiplexer_1_out7), .in({7{1'b1}}), .sel(counter_6_q), .en(in_1));
  Multiplexer #(.select(3), .width(8)) multiplexer_1 (
    .in0(counter_1_q), .in2(counter_4_q), .in4(counter_5_q), .in6(counter_2_q), .in7(counter_3_q),
    .out(multiplexer_1_out), .sel(counter_6_q), .en(in_1));  // open: in1, in3, in5
  BCD7segm bcd7segm_1 (.in_1(multiplexer_1_out), .out_2(bcd7segm_1_out_2));
  assign AND2_3_out = bcd7segm_1_out_2 & demultiplexer_1_out0;  // AND_Gate AND2_3, 7 bits wide
  _7_Segment_Display u_7_segment_display_1 (
    .g(AND2_3_out[6]), .f(AND2_3_out[5]), .a(AND2_3_out[0]), .b(AND2_3_out[1]), .e(AND2_3_out[4]),
    .d(AND2_3_out[3]), .c(AND2_3_out[2]));  // open: dp
  _7_Segment_Display u_7_segment_display_2 (
    .g(AND2_4_out[6]), .f(AND2_4_out[5]), .a(AND2_4_out[0]), .b(AND2_4_out[1]), .e(AND2_4_out[4]),
    .d(AND2_4_out[3]), .c(AND2_4_out[2]));  // open: dp
  assign AND2_4_out = bcd7segm_1_out_2 & demultiplexer_1_out1;  // AND_Gate AND2_4, 7 bits wide
  _7_Segment_Display u_7_segment_display_3 (
    .g(AND2_5_out[6]), .f(AND2_5_out[5]), .a(AND2_5_out[0]), .b(AND2_5_out[1]), .e(AND2_5_out[4]),
    .d(AND2_5_out[3]), .c(AND2_5_out[2]));  // open: dp
  assign AND2_5_out = bcd7segm_1_out_2 & demultiplexer_1_out2;  // AND_Gate AND2_5, 7 bits wide
  _7_Segment_Display u_7_segment_display_4 (
    .g(AND2_6_out[6]), .f(AND2_6_out[5]), .a(AND2_6_out[0]), .b(AND2_6_out[1]), .e(AND2_6_out[4]),
    .d(AND2_6_out[3]), .c(AND2_6_out[2]));  // open: dp
  assign AND2_6_out = bcd7segm_1_out_2 & demultiplexer_1_out3;  // AND_Gate AND2_6, 7 bits wide
  _7_Segment_Display u_7_segment_display_5 (
    .g(AND2_7_out[6]), .f(AND2_7_out[5]), .a(AND2_7_out[0]), .b(AND2_7_out[1]), .e(AND2_7_out[4]),
    .d(AND2_7_out[3]), .c(AND2_7_out[2]));  // open: dp
  assign AND2_7_out = bcd7segm_1_out_2 & demultiplexer_1_out4;  // AND_Gate AND2_7, 7 bits wide
  assign AND2_8_out = bcd7segm_1_out_2 & demultiplexer_1_out5;  // AND_Gate AND2_8, 7 bits wide
  _7_Segment_Display u_7_segment_display_6 (
    .g(AND2_8_out[6]), .f(AND2_8_out[5]), .a(AND2_8_out[0]), .b(AND2_8_out[1]), .e(AND2_8_out[4]),
    .d(AND2_8_out[3]), .c(AND2_8_out[2]));  // open: dp
  assign AND2_9_out = bcd7segm_1_out_2 & demultiplexer_1_out6;  // AND_Gate AND2_9, 7 bits wide
  _7_Segment_Display u_7_segment_display_7 (
    .g(AND2_9_out[6]), .f(AND2_9_out[5]), .a(AND2_9_out[0]), .b(AND2_9_out[1]), .e(AND2_9_out[4]),
    .d(AND2_9_out[3]), .c(AND2_9_out[2]));  // open: dp
  assign AND2_10_out = bcd7segm_1_out_2 & demultiplexer_1_out7;  // AND_Gate AND2_10, 7 bits wide
  _7_Segment_Display u_7_segment_display_8 (
    .g(AND2_10_out[6]), .f(AND2_10_out[5]), .a(AND2_10_out[0]), .b(AND2_10_out[1]), .e(AND2_10_out[4]),
    .d(AND2_10_out[3]), .c(AND2_10_out[2]));  // open: dp

  // Notes on the sheet:
  //   exc7
  //   exc4
  //   clk
  //   exc2
  //   in_zi
  //   OR3_2
  //   exc6
  //   OR2
  //   clk
  //   in_minut
  //   clk
  //   clk
  //   in_grade
  //   exc1
  //   OR3_1
  //   in_luna
  //   clk
  //   ex_zi
  //   counter2
  //   in_ora
  //   clk
  //   counter4
  //   ex_minut.
  //   counter5
  //   comparator1
  //   ex_luna
  //   ex_luna
  //   counter1
  //   exc2
  //   comparator2
  //   counter3
  //   ex_ora
  //   ex_grade
  //   ex_grade
  //   comparator3
  //   comparator5
  //   comparator6
  //   exc6
  //   ex_minut
  //   ex_luna
  //   exc3
  //   exc8
  //   exc5
  //   exc6
  //   ex_ora
  //   exA2_1
  //   AND2_1
  //   exc5
  //   exA2_2
  //   AND2_2
  //   ex_sum
  //   sumator
  //   comparator4
  //   exc4
  //   exc7
  //   comparator7
  //   comparator8
  //   exc8
  //   ex_zi
  //   ex_minut.
  //   counter _afisare
  //   BCD7segm
  //   ex_mux
  //   ex_dcd
  //   ZIUA
  //   ex_dcd1
  //   ex_dcd2
  //   LUNA
  //   ex_dcd3
  //   ex_dcd4
  //   ORA
  //   ex_dcd5
  //   ex_dcd6
  //   MINUTE
  //   ex_dcd7
  //   ex_dcd8
  //   TEMPERATURA
endmodule
